// Digital circuit 2_bit_2_op_alu_scheme.dig as structural Verilog
module _2_bit_2_op_alu_scheme (
  input  Op,
  input  A_1,
  input  A_0,
  input  B_1,
  input  B_0,
  input  B_1_2,
  input  B_0_2,
  input  A_1_2,
  input  A_0_2,
  input  Op_2,
  output OUT_1,
  output OUT_0,
  output OUT_C,
  output OUT_1_2,
  output OUT_0_2,
  output OUT_C_2,
  output out_17,
  output out_18,
  output out_19,
  output out_20
);

  wire _7408_1_pin3, _7408_1_pin6, _74283_1_pin1, _74283_1_pin4, _74283_1_pin13, add_1_c_o, and_1_out,
       and_2_out, multiplexer_1_out, not_1_out;
  wire [1:0] add_1_s;

  not not_1 (not_1_out, 1'b0);
  Multiplexer multiplexer_1 (.sel(Op), .in_0(1'b0), .in_1(not_1_out), .out(multiplexer_1_out));
  and and_1 (and_1_out, A_1, B_1);
  and and_2 (and_2_out, A_0, B_0);
  _7408 _7408_1 (
    .pin1(A_1_2), .pin2(B_1_2), .pin3(_7408_1_pin3), .pin4(A_0_2), .pin5(B_0_2), .pin6(_7408_1_pin6),
    .pin7(1'b0), .pin8(out_18), .pin9(1'b0), .pin10(1'b0), .pin11(out_17), .pin12(1'b0), .pin13(1'b0),
    .pin14(1'b1));
  Add #(.Bits(2)) add_1 (.a({A_1, A_0}), .b({B_1, B_0}), .c_i(1'b0), .s(add_1_s), .c_o(add_1_c_o));
  _74283 _74283_1 (
    .pin1(_74283_1_pin1), .pin2(B_1_2), .pin3(A_1_2), .pin4(_74283_1_pin4), .pin5(A_0_2), .pin6(B_0_2),
    .pin7(1'b0), .pin8(1'b0), .pin9(out_19), .pin11(1'b0), .pin12(1'b0), .pin13(_74283_1_pin13),
    .pin14(1'b0), .pin15(1'b0), .pin16(1'b1));  // open: pin10
  _74257 _74257_1 (
    .pin1(Op_2), .pin2(_7408_1_pin3), .pin3(_74283_1_pin1), .pin4(OUT_1_2), .pin5(_7408_1_pin6),
    .pin6(_74283_1_pin4), .pin7(OUT_0_2), .pin8(1'b0), .pin9(out_20), .pin10(1'b0), .pin11(1'b0),
    .pin12(OUT_C_2), .pin13(_74283_1_pin13), .pin14(1'b0), .pin15(1'b0), .pin16(1'b1));
  Multiplexer multiplexer_2 (.sel(multiplexer_1_out), .in_0(and_1_out), .in_1(add_1_s[1]), .out(OUT_1));
  Multiplexer multiplexer_3 (.sel(multiplexer_1_out), .in_0(and_2_out), .in_1(add_1_s[0]), .out(OUT_0));
  Multiplexer multiplexer_4 (.sel(multiplexer_1_out), .in_0(1'b0), .in_1(add_1_c_o), .out(OUT_C));
endmodule
